# Fritzing sketch CircuitBoard2 (saved by Fritzing 0.9.9b)
circuit board: 9.19304cm x 9.75059cm
breadboards: 1

parts:
  NodeMCU = NodeMCU V1.0 Rev 2
  U2 = Fielect 10k Fader [part_number=FLT20200619M-0036]
  U3 = Fielect 10k Fader [part_number=FLT20200619M-0036]
  Mux = Analog Digital MUX Breakout

nets:
  N1: NodeMCU.3v3, U2.3, U3.3
  GND: NodeMCU.GND, U2.1, U2.GND, U3.1, U3.GND, Mux.GND
  N2: NodeMCU.D3, Mux.S3
  N3: NodeMCU.D2, Mux.S2
  N4: NodeMCU.D1, Mux.S1
  N5: NodeMCU.D0, Mux.S0
  N6: NodeMCU.A0, Mux.SIG
  VIN: NodeMCU.Vin, Mux.VCC
  N7: U2.2, Mux.C0
  N8: U3.2, Mux.C1

custom parts:
  NodeMCU V1.0 Rev 2: ESP8266 based NodeMCU
